# Fritzing sketch Schema (saved by Fritzing 0.9.3b)
circuit board: 24.7238cm x 18.274cm
breadboards: 2

parts:
  M1 = DC Motor
  R2 = Resistor [tolerance=±5% resistance=220 package=THT]
  DS1_-_Temp_1 = DS18B20 1-Wire Temperature Sensor Probe Cable
  YL-83_-_Humd_3 = YL-83 Rain Sensor - Control Board
  DS2_-_Temp_2 = DS18B20 1-Wire Temperature Sensor Probe Cable
  DS3_-_Temp_3 = DS18B20 1-Wire Temperature Sensor Probe Cable
  Q2 = NPN-Transistor [package="TO92 [THT]"]
  Q3 = NPN-Transistor [package="TO92 [THT]"]
  Q4 = NPN-Transistor [package="TO92 [THT]"]
  R3 = Resistor [tolerance=±5% resistance=220 package=THT]
  R4 = Resistor [tolerance=±5% resistance=220 package=THT]
  R5 = Resistor [tolerance=±5% resistance=220 package=THT]
  M2 = DC Motor
  M3 = DC Motor
  M4 = DC Motor
  Q1 = NPN-Transistor [package="TO92 [THT]"]
  R6 = Resistor [tolerance=±5% resistance=4.7k package=THT]
  R7 = Resistor [tolerance=±5% resistance=4.7k package=THT]
  R8 = Resistor [tolerance=±5% resistance=4.7k package=THT]
  YL-83_-_Condensation = YL-83 Rain Sensor - Control Board
  YL-83_-_Humd_2 = YL-83 Rain Sensor - Control Board
  Part1 = Arduino Uno (Rev3)
  YL-83_-_Humd_1 = YL-83 Rain Sensor - Control Board
  YL-83_-_Detection_Board1 = YL-83 Rain Sensor - Detection Board

nets:
  GND: M1.pin_1, DS1_-_Temp_1.GND, DS2_-_Temp_2.GND, DS3_-_Temp_3.GND, M2.pin_1, M3.pin_1, M4.pin_1, Part1.GND
  N1: M1.pin_2, Q1.C
  N2: R2.Pin_0, Q1.B
  N3: R2.Pin_1, Part1.D12/MISO
  VCC: DS1_-_Temp_1.VDD, YL-83_-_Humd_3.VCC, DS2_-_Temp_2.VDD, DS3_-_Temp_3.VDD, R6.Pin_1, R7.Pin_1, R8.Pin_1, YL-83_-_Condensation.VCC, YL-83_-_Humd_2.VCC, Part1.5V, YL-83_-_Humd_1.VCC
  N4: DS1_-_Temp_1.shield, R6.Pin_0, Part1.D13/SCK
  N5: YL-83_-_Humd_3.GND, Part1.D4
  N6: YL-83_-_Humd_3.AO, Part1.A2
  N7: DS2_-_Temp_2.shield, R7.Pin_0, Part1.D8
  N8: DS3_-_Temp_3.shield, R8.Pin_0, Part1.D3_PWM
  N9: Q2.E, Q3.E, Q4.E, Q1.E, Part1.VIN
  N10: Q2.B, R3.Pin_0
  N11: Q2.C, M2.pin_2
  N12: Q3.B, R4.Pin_0
  N13: Q3.C, M3.pin_2
  N14: Q4.B, R5.Pin_0
  N15: Q4.C, M4.pin_2
  N16: R3.Pin_1, Part1.D11_PWM/MOSI
  N17: R4.Pin_1, Part1.D9_PWM
  N18: R5.Pin_1, Part1.D5_PWM
  N19: YL-83_-_Condensation.GND, Part1.D10_PWM/SS
  N20: YL-83_-_Condensation.DO, Part1.D2
  N21: YL-83_-_Condensation.POS, YL-83_-_Detection_Board1.POS
  N22: YL-83_-_Condensation.NEG, YL-83_-_Detection_Board1.NEG
  N23: YL-83_-_Humd_2.GND, Part1.D6_PWM
  N24: YL-83_-_Humd_2.AO, Part1.A1
  N25: Part1.A0, YL-83_-_Humd_1.AO
  N26: Part1.D7, YL-83_-_Humd_1.GND

custom parts:
  YL-83 Rain Sensor - Control Board: The YL-83 is a rain sensor that has more resistance when dry and less resistance when wet. The module runs at 5V.
  YL-83 Rain Sensor - Detection Board: The YL-83 is a rain sensor that has more resistance when dry and less resistance when wet. The module runs at 5V.
